# Fritzing sketch Photoflux (saved by Fritzing 0.9.10b)
breadboards: 1

parts:
  R1 = PHOTOCELL [package=photocell-kit]
  LED1 = smd LED [color="Red (633nm)" package="1206 [SMD]"]
  A1 = Arduino UNO R4 WiFi
  VCC1 = Battery block 9V
  Mod1 = KY-019 5V Relay Module [package="Breakout board"]
  S1 = Taiway 100-SP-X-T1 SPDT Miniature Toggle Switch [part_number=100-SP-X-T1-0-0-B1-M2 package=THT]
  R3 = Resistor [tolerance=±5% power=0.25 resistance=10k package=THT]
  R4 = Rotary Potentiometer (Small) [maximum_resistance=100kΩ knob_status=50% power=0.5W package=THT]

nets:
  N1: R1.P$1, A1.Pin_8, A1.Pin_27, Mod1.+, R4.leg2
  N2: R1.P$2, A1.Pin_12, R3.Pin_0
  N3: LED1.cathode, A1.Pin_9, A1.Pin_10, A1.Pin_30, A1.Pin_48, VCC1.-, Mod1.-, R3.Pin_1, R4.leg1
  N4: LED1.anode, A1.Pin_47
  N5: A1.Pin_11, VCC1.+, S1.L2
  N6: A1.Pin_13, R4.wiper
  N7: A1.Pin_36, Mod1.S
  N8: Mod1.NC, S1.L1

notes:
  Hier ist die Blitzbirne

custom parts:
  Arduino UNO R4 WiFi: The Arduino UNO R4 WiFi merges the RA4M1 microprocessor from Renesas with the ESP32-S3 from Espressif, creating an all-in-one tool for makers with enhanced processing power and a diverse array of new peripherals.
  KY-019 5V Relay Module: KY-019 5V Relay module, used to control AC circuits. (Special thanks to vanepp for fixing the PCB holes and other errors)
